# Fritzing sketch RGBdriverV2 (saved by Fritzing 0.9.3b)
circuit board: 3.59546cm x 2.74716cm
breadboards: 1

parts:
  Q1 = Basic FET N-Channel [package="TO220 [THT]"]
  R1 = Resistor [tolerance=±5% resistance=330 package=THT]
  Power_connector = Screw terminal - 2 pins [package=THT]
  Ledstrip_connector = screw terminal, 4 pins
  Signal_connector_(pwm) = screw terminal, 4 pins
  R2 = Resistor [tolerance=±5% resistance=10k package=THT]
  Q2 = Basic FET N-Channel [part_number=IRLB8721 package="TO220 [THT]"]
  R3 = Resistor [tolerance=±5% resistance=330 package=THT]
  R4 = Resistor [tolerance=±5% resistance=10k package=THT]
  Q3 = Basic FET N-Channel [part_number=IRLB8721 package="TO220 [THT]"]
  R5 = Resistor [tolerance=±5% resistance=10k package=THT]
  R6 = Resistor [tolerance=±5% resistance=330 package=THT]

nets:
  N1: Q1.gate, R1.Pin_0, R5.Pin_0
  R sink: Q1.drain, Ledstrip_connector.pin2
  GND: Q1.source, Power_connector.pin2, Signal_connector_(pwm).pin1, R2.Pin_1, Q2.source, R4.Pin_1, Q3.source, R5.Pin_1
  R signal: R1.Pin_1, Signal_connector_(pwm).pin3
  12V: Power_connector.pin1, Ledstrip_connector.pin4
  B sink: Ledstrip_connector.pin1, Q2.drain
  G sink: Ledstrip_connector.pin3, Q3.drain
  B signal: Signal_connector_(pwm).pin2, R3.Pin_0
  N2: Signal_connector_(pwm).pin4, R6.Pin_1
  N3: R2.Pin_0, R3.Pin_1, Q3.gate
  N4: Q2.gate, R4.Pin_0, R6.Pin_0

notes:
  in
  out
  -
  +
  By Paul-Ver
  RGB ledstrip controller
  3x max 30V sink
  16A/ch if heatsink
  3x PWM input
  0-30V
  2.5V to 5V logic
